# Fritzing sketch IOT project.ino (saved by Fritzing 0.9.5d)
circuit board: 8.46667cm x 5.64444cm

parts:
  Part1 = RFID-RC522-v2
  Part2 = Arduino Uno (Rev3)
  J1 = Piezo Speaker
  Display1 = LCD screen 16x2 IIC [part_number=101290]

nets:
  N1: Part1.SDA, Part2.D10_PWM/SS
  N2: Part1.SCK, Part2.D13/SCK
  N3: Part1.MOSI, Part2.D11_PWM/MOSI
  N4: Part1.MISO, Part2.D12/MISO
  GND: Part1.GND, Part2.GND, J1.pin1, Display1.GND
  N5: Part1.RST, Part2.D9_PWM
  3.3V: Part1.3.3V, Part2.3V3
  N6: Part2.A4/SDA, Display1.SDA
  N7: Part2.A5/SCL, Display1.SCL
  N8: Part2.D8, J1.pin2
  5V: Part2.5V, Display1.VCC

custom parts:
  RFID-RC522-v2: A simple China made RFID-RC522 Reader; do check the pin labels, as this is a MFRC522 based clone.
  LCD screen 16x2 IIC: LCD screen with HD44780 controller enables showing text, symbols, value or anything else that comes from Croduino/Arduino. It is capable of showing 16 symbols in two lines and therefore can be used in many projects that need to send clearly visible and legible output information.. • Color of symbols: White • Backlight: Blue • Dimensions: 80 x 36 x 12 mm • Screen dimensions: 64.5 x 16 mm •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
